# Fritzing sketch LR1 (saved by Fritzing 0.9.5d)
breadboards: 1

parts:
  R3 = Resistor [tolerance=±5% resistance=10k package=THT]
  R4 = Resistor [tolerance=±5% resistance=10k package=THT]
  S5 = Pushbutton [package=THT]
  S6 = Pushbutton [package=THT]
  S7 = Pushbutton [package=THT]
  VCC1 = Battery
  LED1 = LED - 5mm [color="Red (633nm)" package="5 mm [THT]"]
  R1 = Resistor [tolerance=±5% resistance=330 package=THT]
  1 = Arduino Micro (Rev3)
  R2 = Resistor [tolerance=±5% resistance=10k package=THT]

nets:
  N1: R3.Pin_0, S6.leg1, 1.D10_PWM/A10
  N2: R3.Pin_1, R4.Pin_1, VCC1.-, R2.Pin_1
  N3: R4.Pin_0, S7.leg1, 1.D9_PWM/A9
  N4: S5.leg0, S6.leg0, S7.leg0, VCC1.+
  N5: S5.leg1, 1.D11_PWM, R2.Pin_0
  N6: LED1.cathode, 1.GND
  N7: LED1.anode, R1.Pin_1
  N8: R1.Pin_0, 1.D13_PWM
